# Fritzing sketch esp32 (saved by Fritzing 0.9.10b)
breadboards: 1

parts:
  RE1 = KY-040 Rotary encoder [package="Breakout board"]
  M1 = ESP32-S2-DevKitC-1 [part_number=ESP32-S2-DevKitC-1]

nets:
  N1: RE1.GND, M1.pin_22, M1.pin_23, M1.pin_24, M1.pin_44
  N2: RE1.Vcc, M1.pin_4
  N3: RE1.DT, M1.pin_10
  N4: RE1.CLK, M1.pin_9
  N5: M1.pin_1, M1.pin_2

custom parts:
  KY-040 Rotary encoder: KY-040 Rotary Encoder with switch on breakout borad from AZ Delivery
  ESP32-S2-DevKitC-1: ESP32-S2-DevKitC-1 is an entry-level development board based on ESP32-S2-SOLO (on-board PCB antenna). It is based on the ESP32 microcontroller that boasts Wifi, Bluetooth, Ethernet and Low Power support all in a single chip. (vanepp) Feb 2022: converted to ESP32-S2-DevKitC-1. This module is 44pins long (2x22) and 11 pins width.
